# Fritzing sketch manual-test-bench (saved by Fritzing 1.0.3b)
breadboards: 1

parts:
  Part1 = Arduino Uno (Rev3)
  Raspberry_Pi_1 = Raspberry Pi 3 [part_number=RPI-3-V1.2]  # not connected
  CONN1 = USB connector [package=THT]
  CONN2 = USB connector [package=THT]
  S1 = Pushbutton [package="[THT]"]
  S2 = Pushbutton [package="[THT]"]
  YF-S201_Flow_Meter1 = YF-S201 Water Flow Meter

nets:
  N1: Part1.D2, YF-S201_Flow_Meter1.SIG
  N2: Part1.D3_PWM, S1.Pin_1, S1.Pin_2
  N3: Part1.D4, S2.Pin_1, S2.Pin_2
  5V: Part1.5V, YF-S201_Flow_Meter1.VCC
  5V_2: CONN1.5V, CONN2.5V
  N4: CONN1.d-, CONN2.d-
  N5: CONN1.d+, CONN2.d+
  N6: CONN1.GND, CONN1.chassis5, CONN2.chassis5, CONN2.chassis6
  N7: S1.Pin_3, S1.Pin_4, S2.Pin_3, S2.Pin_4, YF-S201_Flow_Meter1.GND

custom parts:
  YF-S201 Water Flow Meter: The YF-S201 Flow Meter. The input voltage is 5V to 24V (DC).
